# Fritzing sketch light_controls (saved by Fritzing 0.9.3b)
breadboards: 1

parts:
  Part1 = Arduino Nano (Rev3.0)
  ULN1 = Darlington Driver [package=dil18]
  ULN2 = Darlington Driver [package=dil18]
  BAT1 = BC9VPC [package=bc9vpc]
  LED1 = smd LED [color="Red (633nm)" package="0805 [SMD]"]
  LED2 = LED - 5mm [color="Red (633nm)" package="5 mm [THT]"]
  LED3 = smd LED [color="Red (633nm)" package="0805 [SMD]"]
  LED4 = smd LED [color="Red (633nm)" package="0805 [SMD]"]
  LED5 = smd LED [color="Red (633nm)" package="0805 [SMD]"]
  LED6 = LED - 5mm [color="Red (633nm)" package="5 mm [THT]"]
  LED7 = LED - 5mm [color="Red (633nm)" package="5 mm [THT]"]
  LED8 = LED - 5mm [color="Red (633nm)" package="5 mm [THT]"]
  LED9 = LED - 5mm [color="Red (633nm)" package="5 mm [THT]"]
  LED10 = LED - 5mm [color="Red (633nm)" package="5 mm [THT]"]
  LED11 = LED - 5mm [color="Red (633nm)" package="5 mm [THT]"]
  LED12 = LED - 5mm [color="Red (633nm)" package="5 mm [THT]"]
  LED13 = LED - 5mm [color="Red (633nm)" package="5 mm [THT]"]
  LED14 = LED - 5mm [color="Red (633nm)" package="5 mm [THT]"]
  LED15 = smd LED [color="Red (633nm)" package="0805 [SMD]"]
  LED16 = smd LED [color="Red (633nm)" package="0805 [SMD]"]

nets:
  N1: Part1.GND, ULN1.9, ULN2.9, BAT1.V-
  N2: Part1.D2, ULN1.1
  N3: Part1.D3, ULN1.2
  N4: Part1.D4, ULN1.3
  N5: Part1.D5, ULN1.4
  N6: Part1.D6, ULN1.5
  N7: Part1.D7, ULN1.6
  N8: Part1.D8, ULN1.7
  N9: Part1.D9, ULN1.8
  N10: Part1.D10, ULN2.1
  N11: Part1.D11/MOSI, ULN2.2
  N12: Part1.D12/MISO, ULN2.3
  N13: Part1.A3, ULN2.8
  N14: Part1.A2, ULN2.7
  N15: Part1.A1, ULN2.6
  N16: Part1.A0, ULN2.5
  N17: Part1.D13/SCK, ULN2.4
  N18: ULN1.11, LED7.cathode
  N19: ULN1.12, LED6.cathode
  N20: ULN1.13, LED5.cathode
  N21: ULN1.14, LED4.cathode
  N22: ULN1.15, LED3.cathode
  N23: ULN1.16, LED2.cathode
  N24: ULN1.17, LED1.cathode
  N25: ULN1.18, LED16.cathode
  N26: ULN2.11, LED15.cathode
  N27: ULN2.12, LED14.cathode
  N28: ULN2.13, LED13.cathode
  N29: ULN2.14, LED12.cathode
  N30: ULN2.15, LED11.cathode
  N31: ULN2.16, LED10.cathode
  N32: ULN2.17, LED9.cathode
  N33: ULN2.18, LED8.cathode
  N34: BAT1.V+, LED1.anode, LED2.anode, LED3.anode, LED4.anode, LED5.anode, LED6.anode, LED7.anode, LED8.anode, LED9.anode, LED10.anode, LED11.anode, LED12.anode, LED13.anode, LED14.anode, LED15.anode, LED16.anode
